# Fritzing sketch handkontroller (saved by Fritzing 0.9.8b)
stripboards: 1

parts:
  Part1 = Arduino Nano (Rev3.0) (ICSP)
  J1 = Screw terminal - 2 pins [package=THT]  # not connected
  J2 = Screw terminal - 2 pins [package=THT]  # not connected
  J3 = Screw terminal - 2 pins [package=THT]

nets:
  N1: Part1.GND, J3.pin1
  N2: Part1.5V, J3.pin2
